// Logisim project flopFlip.circ as structural Verilog
module main (
  input  [1:0] in_1,
  input  in_2,
  input  in_3,
  input  [3:0] in_4,
  input  in_5,
  output [3:0] out_6
);

  Registrador_completo_VHDL registrador_completo_vhdl_1 (
    .sel(in_1), .j(in_2), .clock(in_3), .p(in_4), .clear(in_5), .Q(out_6));
endmodule

module JKME (
  input  SET,
  input  J,
  input  CLOCK,
  input  K,
  input  RESET,
  output Q,
  output NQ
);

  wire nand_1_out, nand_2_out, nand_3_out, nand_4_out, nand_5_out, nand_6_out, not_1_out;

  nand nand_1 (nand_1_out, CLOCK, J, NQ);
  nand nand_2 (nand_2_out, Q, K, CLOCK);
  not not_1 (not_1_out, CLOCK);
  nand nand_3 (nand_3_out, SET, nand_1_out, nand_4_out);
  nand nand_4 (nand_4_out, nand_3_out, nand_2_out, RESET);
  nand nand_5 (nand_5_out, nand_3_out, not_1_out);
  nand nand_6 (nand_6_out, not_1_out, nand_4_out);
  nand nand_7 (Q, SET, nand_5_out, NQ);
  nand nand_8 (NQ, Q, nand_6_out, RESET);
endmodule

module FFT (
  input  SET,
  input  J,
  input  clk,
  input  CLEAR,
  output Q,
  output NQ
);

  JKME jkme_1 (.SET(SET), .J(J), .CLOCK(clk), .K(J), .RESET(CLEAR), .Q(Q), .NQ(NQ));
endmodule

// D
module FFMEPSD (
  input  SET,
  input  J,
  input  CLK,
  input  CLEAR,
  output Q,
  output NQ
);

  wire not_1_out;

  not not_1 (not_1_out, J);
  JKME jkme_1 (.SET(SET), .J(J), .CLOCK(CLK), .K(not_1_out), .RESET(CLEAR), .Q(Q), .NQ(NQ));
endmodule

module conversor (
  input  AA,
  input  BB,
  input  CC,
  input  DD,
  output a,
  output b,
  output c,
  output d,
  output e,
  output f,
  output g
);

  wire and_1_out, and_2_out, and_3_out, and_4_out, and_5_out, and_6_out, and_7_out, and_8_out, and_9_out,
       and_10_out, and_11_out, and_12_out, and_13_out, and_14_out, and_15_out, and_16_out, and_17_out,
       and_18_out, and_19_out, and_20_out, and_21_out, and_22_out, and_23_out, and_24_out, and_25_out,
       and_26_out, and_27_out, and_28_out, and_29_out, and_30_out, and_31_out, and_32_out, and_33_out,
       and_34_out, and_35_out, not_1_out, not_2_out, not_3_out, not_4_out;

  not not_1 (not_1_out, AA);
  not not_2 (not_2_out, BB);
  not not_3 (not_3_out, CC);
  not not_4 (not_4_out, DD);
  and and_1 (and_1_out, not_2_out, not_4_out);
  and and_2 (and_2_out, not_1_out, CC);
  and and_3 (and_3_out, not_1_out, BB, DD);
  and and_4 (and_4_out, AA, not_2_out, not_3_out);
  and and_5 (and_5_out, AA, not_4_out);
  and and_6 (and_6_out, BB, CC);
  and and_7 (and_7_out, not_1_out, not_3_out, not_4_out);
  and and_8 (and_8_out, not_1_out, CC, DD);
  and and_9 (and_9_out, not_2_out, not_4_out);
  and and_10 (and_10_out, AA, not_3_out, DD);
  and and_11 (and_11_out, not_1_out, not_2_out);
  and and_12 (and_12_out, not_1_out, BB);
  and and_13 (and_13_out, AA, not_2_out);
  and and_14 (and_14_out, not_3_out, DD);
  and and_15 (and_15_out, not_2_out, not_3_out);
  and and_16 (and_16_out, not_2_out, DD);
  and and_17 (and_17_out, BB, not_3_out, DD);
  and and_18 (and_18_out, not_1_out, not_2_out, not_4_out);
  and and_19 (and_19_out, not_2_out, CC, DD);
  and and_20 (and_20_out, AA, not_3_out);
  and and_21 (and_21_out, BB, CC, not_4_out);
  and and_22 (and_22_out, not_2_out, not_4_out);
  and and_23 (and_23_out, CC, not_4_out);
  and and_24 (and_24_out, AA, CC);
  and and_25 (and_25_out, AA, BB);
  and and_26 (and_26_out, not_3_out, not_4_out);
  and and_27 (and_27_out, not_1_out, BB, not_3_out);
  and and_28 (and_28_out, BB, not_4_out);
  and and_29 (and_29_out, AA, not_2_out);
  and and_30 (and_30_out, AA, CC);
  and and_31 (and_31_out, not_2_out, CC);
  and and_32 (and_32_out, AA, not_2_out);
  and and_33 (and_33_out, not_1_out, BB, not_3_out);
  and and_34 (and_34_out, CC, not_4_out);
  and and_35 (and_35_out, AA, DD);
  or or_1 (a, and_1_out, and_2_out, and_3_out, and_4_out, and_5_out, and_6_out);
  or or_2 (b, and_7_out, and_8_out, and_9_out, and_10_out, and_11_out);
  or or_3 (c, and_12_out, and_13_out, and_14_out, and_15_out, and_16_out);
  or or_4 (d, and_17_out, and_18_out, and_19_out, and_20_out, and_21_out);
  or or_5 (e, and_22_out, and_23_out, and_24_out, and_25_out);
  or or_6 (f, and_26_out, and_27_out, and_28_out, and_29_out, and_30_out);
  or or_7 (g, and_31_out, and_32_out, and_33_out, and_34_out, and_35_out);
endmodule

module Registrador (
  input  in_1,
  input  in_2,
  input  in_3,
  input  in_4,
  input  in_5,
  input  in_6,
  output out_7,
  output out_8,
  output out_9,
  output out_10
);

  wire and_1_out, and_2_out, and_3_out, and_4_out, and_5_out, and_6_out, and_7_out, and_8_out, button_1_out,
       button_2_out, conversor_1_a, conversor_1_b, conversor_1_c, conversor_1_d, conversor_1_e,
       conversor_1_f, conversor_1_g, not_1_out, not_2_out, not_3_out, not_4_out, not_5_out, not_6_out,
       not_7_out, not_8_out, or_1_out, or_2_out, or_3_out, or_4_out;

  Button button_1 (.out(button_1_out));
  Button button_2 (.out(button_2_out));
  and and_1 (and_1_out, button_1_out, in_1);
  not not_1 (not_1_out, and_1_out);
  and and_2 (and_2_out, ~in_1, button_1_out);  // AND_Gate
  or or_1 (or_1_out, and_2_out, button_2_out);
  not not_2 (not_2_out, or_1_out);
  FFMEPSD ffmepsd_1 (.J(in_5), .CLK(in_6), .SET(not_1_out), .CLEAR(not_2_out), .Q(out_7));  // open: NQ
  and and_3 (and_3_out, button_1_out, in_3);
  and and_4 (and_4_out, ~in_3, button_1_out);  // AND_Gate
  or or_2 (or_2_out, and_4_out, button_2_out);
  not not_3 (not_3_out, and_3_out);
  FFMEPSD ffmepsd_2 (.J(out_7), .CLK(in_6), .SET(not_3_out), .CLEAR(not_4_out), .Q(out_8));  // open: NQ
  not not_4 (not_4_out, or_2_out);
  and and_5 (and_5_out, ~in_4, button_1_out);  // AND_Gate
  and and_6 (and_6_out, button_1_out, in_4);
  not not_5 (not_5_out, and_6_out);
  or or_3 (or_3_out, and_5_out, button_2_out);
  not not_6 (not_6_out, or_3_out);
  FFMEPSD ffmepsd_3 (.J(out_8), .CLK(in_6), .SET(not_5_out), .CLEAR(not_6_out), .Q(out_9));  // open: NQ
  and and_7 (and_7_out, button_1_out, in_2);
  not not_7 (not_7_out, and_7_out);
  and and_8 (and_8_out, ~in_2, button_1_out);  // AND_Gate
  or or_4 (or_4_out, and_8_out, button_2_out);
  not not_8 (not_8_out, or_4_out);
  FFMEPSD ffmepsd_4 (.J(out_9), .CLK(in_6), .SET(not_7_out), .CLEAR(not_8_out), .Q(out_10));  // open: NQ
  conversor conversor_1 (
    .AA(out_7), .BB(out_8), .CC(out_9), .DD(out_10), .a(conversor_1_a), .b(conversor_1_b), .c(conversor_1_c),
    .d(conversor_1_d), .e(conversor_1_e), .f(conversor_1_f), .g(conversor_1_g));
  _7_Segment_Display u_7_segment_display_1 (
    .g(conversor_1_g), .f(conversor_1_f), .a(conversor_1_a), .b(conversor_1_b), .e(conversor_1_e),
    .d(conversor_1_d), .c(conversor_1_c));  // open: dp
endmodule

module mux (
  input  Entrada1,
  input  Entrada2,
  input  sel,
  output out_4
);

  wire and_1_out, and_2_out;

  and and_1 (and_1_out, Entrada1, ~sel);  // AND_Gate
  and and_2 (and_2_out, Entrada2, sel);
  or or_1 (out_4, and_1_out, and_2_out);
endmodule

// MUX
module mux2 (
  input  C0,
  input  in_2,
  input  C1,
  input  in_4,
  input  in_5,
  input  in_6,
  output out_7
);

  wire mux_1_out_4, mux_2_out_4;

  mux mux_1 (.Entrada1(in_2), .Entrada2(in_4), .sel(C0), .out_4(mux_1_out_4));
  mux mux_2 (.Entrada1(in_5), .Entrada2(in_6), .sel(C0), .out_4(mux_2_out_4));
  mux mux_3 (.Entrada1(mux_1_out_4), .Entrada2(mux_2_out_4), .sel(C1), .out_4(out_7));
endmodule

module Registrador_completo (
  input  I2,
  input  I1,
  input  I0,
  input  I3,
  input  C1,
  input  C0,
  input  J,
  input  CK,
  input  clear,
  output out_10,
  output out_11,
  output out_12,
  output out_13
);

  wire mux2_1_out_7, mux2_2_out_7, mux2_3_out_7, mux2_4_out_7;

  mux2 mux2_1 (.in_2(out_10), .in_4(out_11), .in_5(J), .in_6(I3), .C0(C0), .C1(C1), .out_7(mux2_1_out_7));
  FFMEPSD ffmepsd_1 (.J(mux2_1_out_7), .CLK(CK), .SET(1'b1), .CLEAR(clear), .Q(out_10));  // open: NQ
  mux2 mux2_2 (.in_2(out_11), .in_4(out_12), .in_5(out_10), .in_6(I2), .C0(C0), .C1(C1), .out_7(mux2_2_out_7));
  FFMEPSD ffmepsd_2 (.J(mux2_2_out_7), .CLK(CK), .SET(1'b1), .CLEAR(clear), .Q(out_11));  // open: NQ
  mux2 mux2_3 (.in_2(out_12), .in_4(out_13), .in_5(out_11), .in_6(I1), .C0(C0), .C1(C1), .out_7(mux2_3_out_7));
  FFMEPSD ffmepsd_3 (.J(mux2_3_out_7), .CLK(CK), .SET(1'b1), .CLEAR(clear), .Q(out_12));  // open: NQ
  mux2 mux2_4 (.in_2(out_13), .in_4(J), .in_5(out_12), .in_6(I0), .C0(C0), .C1(C1), .out_7(mux2_4_out_7));
  FFMEPSD ffmepsd_4 (.J(mux2_4_out_7), .CLK(CK), .SET(1'b1), .CLEAR(clear), .Q(out_13));  // open: NQ
endmodule

// VHDL entity Registrador_completo_VHDL, as the project stores it:
LIBRARY ieee;
USE ieee.std_logic_1164.all;

ENTITY Registrador_completo_VHDL IS
  PORT (
  ------------------------------------------------------------------------------
    sel      : IN  std_logic_vector(1 DOWNTO 0);  -- Select mode                  
    j        : IN  std_logic;                    -- Input for shift operations
    clock    : IN std_logic;                     -- Clock signal
    p        : IN std_logic_vector(3 downto 0);               -- Parallel inputs
    clear    : IN std_logic;                     -- Asynchronous clear
  ------------------------------------------------------------------------------
    Q        : OUT std_logic_vector(3 DOWNTO 0)  -- Outputs
  ------------------------------------------------------------------------------
  );
END Registrador_completo_VHDL;

ARCHITECTURE TypeArchitecture OF Registrador_completo_VHDL IS
    signal REG : STD_LOGIC_VECTOR(3 DOWNTO 0) := "0000";
BEGIN
    PROCESS(clock, clear)
    BEGIN
        IF clear = '1' THEN
            REG <= "0000"; 

        ELSIF rising_edge(clock) THEN
            CASE sel IS
                WHEN "00" =>
                    REG <= REG;
                WHEN "01" =>
                    REG <= j & REG(3 DOWNTO 1);
                WHEN "10" =>
                    REG <= REG(2 DOWNTO 0) & j;
                WHEN "11" =>
                    REG <= p;
                    
                WHEN OTHERS =>
                    REG <= REG;  -- Default case
            END CASE;
        END IF;
    END PROCESS;

    Q <= REG;

END TypeArchitecture;

// VHDL entity jk_mestre_escravo, as the project stores it:
library IEEE;
use IEEE.STD_LOGIC_1164.ALL;

entity jk_mestre_escravo is
    Port (
        J      : in STD_LOGIC;        -- Entrada J
        K      : in STD_LOGIC;        -- Entrada K
        CLK    : in STD_LOGIC;        -- Clock
        PRESET : in STD_LOGIC;        -- Entrada de preset assíncrono
        CLEAR  : in STD_LOGIC;        -- Entrada de clear assíncrono
        Q      : out STD_LOGIC;       -- Saída Q
        QN     : out STD_LOGIC        -- Saída negada (Q barrado)
    );
end jk_mestre_escravo;

architecture Behavioral of jk_mestre_escravo is
    signal master_q : STD_LOGIC := '0'; -- Estado interno do flip-flop mestre
begin
    process(CLK, PRESET, CLEAR)
    begin
        -- Comportamento assíncrono de preset e clear
        if (CLEAR = '0') then
            master_q <= '0';
        elsif (PRESET = '0') then
            master_q <= '1';
        elsif rising_edge(CLK) then
            -- Flip-Flop Mestre
            if (J = '0' and K = '1') then
                master_q <= '0'; -- Reset
            elsif (J = '1' and K = '0') then
                master_q <= '1'; -- Set
            elsif (J = '1' and K = '1') then
                master_q <= NOT master_q; -- Toggle
            end if;
        end if;
    end process;

    -- Flip-Flop Escravo
    process(CLK, PRESET, CLEAR)
    begin
        -- Comportamento assíncrono de preset e clear
        if (CLEAR = '0') then
            Q <= '0';
            QN <= '1';
        elsif (PRESET = '0') then
            Q <= '1';
            QN <= '0';
        elsif falling_edge(CLK) then
            -- Escravo segue o estado do mestre no ciclo do clock
            Q <= master_q;
            QN <= NOT master_q;
        end if;
    end process;
end Behavioral;

// VHDL entity MUX2_VHDL, as the project stores it:
--------------------------------------------------------------------------------
-- Project :
-- File    :
-- Autor   :
-- Date    :
--
--------------------------------------------------------------------------------
-- Description :
--
--------------------------------------------------------------------------------

LIBRARY ieee;
USE ieee.std_logic_1164.all;

ENTITY MUX2_VHDL IS
  PORT (
  ------------------------------------------------------------------------------
  --Insert input ports below
    sel      : IN  std_logic_vector(1 downto 0);               
    A        : IN  std_logic;
    B        : IN  std_logic;
    C        : IN  std_logic;
    D        : IN  std_logic;
  ------------------------------------------------------------------------------
  --Insert output ports below
    RES        : OUT std_logic            
    );
END MUX2_VHDL;

--------------------------------------------------------------------------------
--Complete your VHDL description below
--------------------------------------------------------------------------------

ARCHITECTURE TypeArchitecture OF MUX2_VHDL IS

BEGIN
	process (sel,A,B,C,D)
	BEGIN
		IF SEL = "00" THEN
			RES <= A;
		ELSIF SEL = "01" THEN
			RES <= B;
		ELSIF SEL = "10" THEN
			RES <= C;
		ELSIF SEL = "11" THEN
			RES <= D;
		END IF;
	END PROCESS;
			

END TypeArchitecture;

// VHDL entity Registrador_VHDL, as the project stores it:
LIBRARY ieee;
USE ieee.std_logic_1164.all;

ENTITY Registrador_VHDL IS
  PORT (
  ------------------------------------------------------------------------------
    sel      : IN  std_logic_vector(1 DOWNTO 0);  -- Select mode                  
    j        : IN  std_logic;                    -- Input for shift operations
    clock    : IN std_logic;                     -- Clock signal
    p        : IN std_logic_vector(3 downto 0);               -- Parallel inputs
    clear    : IN std_logic;                     -- Asynchronous clear
  ------------------------------------------------------------------------------
    Q        : OUT std_logic_vector(3 DOWNTO 0)  -- Outputs
  ------------------------------------------------------------------------------
  );
END Registrador_VHDL;

ARCHITECTURE TypeArchitecture OF Registrador_VHDL IS
    signal REG : STD_LOGIC_VECTOR(3 DOWNTO 0) := "0000";
BEGIN
    PROCESS(clock, clear)
    BEGIN
        IF clear = '1' THEN
            REG <= "0000"; 

        ELSIF rising_edge(clock) THEN
            CASE sel IS
                WHEN "00" =>
                    REG <= REG;
                WHEN "01" =>
                    REG <= j & REG(3 DOWNTO 1);
                WHEN "10" =>
                    REG <= REG(2 DOWNTO 0) & j;
                WHEN "11" =>
                    REG <= p;
                    
                WHEN OTHERS =>
                    REG <= REG;  -- Default case
            END CASE;
        END IF;
    END PROCESS;

    Q <= REG;

END TypeArchitecture;
